# Fritzing sketch program_esp8266 (saved by Fritzing 0.9.1b)
breadboards: 1

parts:
  U1 = ESP8266 WiFi Module [part_number=ESP8266]
  Part2 = Arduino Nano (Rev3.0)
  Part3 = FTDI Basic Programmer
  Part4 = Logic Level Converter

nets:
  N1: U1.RXD, Part4.RX_LV
  VCC: U1.VCC, Part2.3V3, Part4.LV
  GND: U1.GPIO_0, U1.GND, Part2.GND, Part4.GND
  N2: U1.CH_PD, Part4.RX2_LV
  N3: U1.TXD, Part4.TX_LV
  N4: Part2.5V, Part4.HV, Part4.RX2_HV
  N5: Part3.RXI, Part4.TX_HV
  N6: Part3.TXO, Part4.RX_HV

notes:
  Program ESP Serial

custom parts:
  ESP8266 WiFi Module: Generic WiFi Module based on the ESP8266 with onboard PCB antenna and UART communications
